// Logisim project cpu.circ as structural Verilog: 3 circuits, main circuit main
module main (
);

  ROM rom_1 ();  // open: addr, data, sel
endmodule

module alu (
  input  [7:0] input1,
  input  [7:0] input2,
  input  [3:0] control,
  output [7:0] \output ,
  output c1,
  output c2,
  output c3
);

  wire [7:0] adder_1_out, and_1_out, multiplier_1_out, not_1_out, or_1_out, subtractor_1_out;

  Adder adder_1 (.a(input1), .b(input2), .out(adder_1_out));  // open: cin, cout
  Subtractor subtractor_1 (.a(input1), .b(input2), .out(subtractor_1_out));  // open: bin, bout
  Multiplier multiplier_1 (.a(input1), .b(input2), .out(multiplier_1_out));  // open: cin, cout
  assign and_1_out = input1 & input2;  // AND_Gate and_1, 8 bits wide
  assign or_1_out = input1 | input2;  // OR_Gate or_1, 8 bits wide
  assign not_1_out = ~input1;  // NOT_Gate not_1, 8 bits wide
  Comparator comparator_1 (.a(input1), .b(input2), .gt(c1), .eq(c2), .lt(c3));
  Multiplexer #(.select(4), .width(8), .enable("false")) multiplexer_1 (
    .in0(adder_1_out), .in1(subtractor_1_out), .in2(multiplier_1_out), .in3(and_1_out), .in4(or_1_out),
    .in5(not_1_out), .out(\output ), .sel(control));  // open: in6, in7, in8, in9, in10, in11, in12, in13, in14, in15
endmodule

module PC (
  input  load,
  input  [7:0] \input ,
  input  increment,
  input  reset,
  output [7:0] out_5
);

  wire not_1_out, or_1_out;

  not not_1 (not_1_out, load);
  Counter counter_1 (
    .load(load), .D(\input ), .count(not_1_out), .Q(out_5), .clk(or_1_out), .clr(reset));  // open: carry
  or or_1 (or_1_out, load, increment);
endmodule
